# Fritzing sketch cooler (saved by Fritzing 0.9.3b)
breadboards: 1

parts:
  DS1 = DS18B20 1-Wire Temperature Sensor [part_number=DS18B20]
  External_Pullup = Resistor [tolerance=±5% resistance=4.7k package="0603 [SMD]"]
  U1 = ATMEGA32U4 [package=qfn]
  FAN = IC, DIP package, 4 pins [chip_label=IC]
  Traco_Power_Supply = SO08-EIAJ [chip_label=THD-12WI package=SO]

nets:
  GND/Supply GND: DS1.GND, U1.GND, FAN.pin2, Traco_Power_Supply.3, Traco_Power_Supply.5, Traco_Power_Supply.7
  Pin 7: DS1.DQ, External_Pullup.Pin_0, U1.PD7(ADC10)
  VDD: DS1.VDD, External_Pullup.Pin_1, U1.VCC
  N1: U1.VBUS, Traco_Power_Supply.8
  Pin 9: U1.PB5(ADC12), FAN.pin4
  24V: FAN.pin1, Traco_Power_Supply.6
  N2: Traco_Power_Supply.1, Traco_Power_Supply.2
